# Fritzing sketch ArdThrottle (saved by Fritzing 0.9.3b)
stripboards: 1

parts:
  Arduino_MEGA_2560 = Arduino Mega 2560 (Rev3)
  LED5 = LED - 5mm [color="Green (570nm)" part_number="Gear Down L" package="5 mm [THT]"]
  LED2 = LED - 5mm [color="Red (633nm)" part_number="Gear Un Safe L" package="5 mm [THT]"]
  U1 = POT [part_number="Speed Brake" package=pot_alpha_rv16af-20]
  U2 = POT [part_number="Throttle L" package=pot_alpha_rv16af-20]
  U3 = POT [part_number="Throttle R" package=pot_alpha_rv16af-20]
  U4 = POT [part_number=Propeller package=pot_alpha_rv16af-20]
  U5 = POT [part_number=Mixture package=pot_alpha_rv16af-20]
  R1 = Resistor [tolerance=±5% resistance=10k package=THT]
  C1 = Capacitor [part_number=104 package=cap-pth-small2]
  R2 = Resistor [tolerance=±5% resistance=10k package=THT]
  R3 = Resistor [tolerance=±5% resistance=10k package=THT]
  R4 = Resistor [tolerance=±5% resistance=10k package=THT]
  R5 = Resistor [tolerance=±5% resistance=10k package=THT]
  R6 = Resistor [tolerance=±5% resistance=10k package=THT]
  C2 = Capacitor [part_number=104 package=cap-pth-small2]
  C3 = Capacitor [part_number=104 package=cap-pth-small2]
  C4 = Capacitor [part_number=104 package=cap-pth-small2]
  C5 = Capacitor [part_number=104 package=cap-pth-small2]
  U6 = POT [part_number=Flaps package=pot_alpha_rv16af-20]
  C6 = Capacitor [part_number=104 package=cap-pth-small2]
  R7 = Resistor [tolerance=±5% resistance=470 package=THT]
  R8 = Resistor [tolerance=±5% resistance=470 package=THT]
  R9 = Resistor [tolerance=±5% resistance=470 package=THT]
  R10 = Resistor [tolerance=±5% resistance=470 package=THT]
  R11 = Resistor [tolerance=±5% resistance=470 package=THT]
  R14 = Resistor [tolerance=±5% resistance=470 package=THT]
  LED1 = LED - 5mm [color="Red (633nm)" part_number="Parking Brake" package="5 mm [THT]"]
  LED4 = LED - 5mm [color="Red (633nm)" part_number="Gear Un Safe R" package="5 mm [THT]"]
  LED3 = LED - 5mm [color="Red (633nm)" part_number="Gear Un Safe Nose" package="5 mm [THT]"]
  LED7 = LED - 5mm [color="Green (570nm)" part_number="Gear Down R" package="5 mm [THT]"]
  LED6 = LED - 5mm [color="Green (570nm)" part_number="Gear Down Nose" package="5 mm [THT]"]
  R12 = Resistor [tolerance=±5% resistance=470 package=THT]
  R15 = Resistor [tolerance=±5% resistance=10k package=THT]
  S1 = Pushbutton [part_number=A/T package="[THT]"]
  C7 = Capacitor [part_number=104 package=cap-pth-small2]
  C8 = Capacitor [part_number=104 package=cap-pth-small2]
  S2 = Pushbutton [part_number=Reverse package="[THT]"]
  R16 = Resistor [tolerance=±5% resistance=10k package=THT]

nets:
  N1: Arduino_MEGA_2560.A0, R1.Pin_0
  N2: Arduino_MEGA_2560.A1, R2.Pin_0
  N3: Arduino_MEGA_2560.A2, R3.Pin_0
  N4: Arduino_MEGA_2560.A3, R4.Pin_0
  N5: Arduino_MEGA_2560.A4, R5.Pin_0
  N6: Arduino_MEGA_2560.A5, R6.Pin_0
  N7: Arduino_MEGA_2560.GND, LED5.cathode, LED2.cathode, U1.A, U2.A, U3.A, U4.A, U5.A, C1.2, C2.2, C3.2, C4.2, C5.2, U6.A, C6.2, LED1.cathode, LED4.cathode, LED3.cathode, LED7.cathode, LED6.cathode, R15.Pin_0, R16.Pin_0
  N8: Arduino_MEGA_2560.D8_PWM, R12.Pin_1
  N9: Arduino_MEGA_2560.D2_PWM, R14.Pin_1
  N10: Arduino_MEGA_2560.D3_PWM, R11.Pin_1
  N11: Arduino_MEGA_2560.D4_PWM, R9.Pin_1
  N12: Arduino_MEGA_2560.D5_PWM, R10.Pin_1
  N13: Arduino_MEGA_2560.D6_PWM, R8.Pin_1
  N14: Arduino_MEGA_2560.D7_PWM, R7.Pin_1
  N15: Arduino_MEGA_2560.5V, U1.E, U2.E, U3.E, U4.E, U5.E, U6.E, S1.Pin_1, S1.Pin_2, C7.2, C8.2, S2.Pin_1, S2.Pin_2
  N16: Arduino_MEGA_2560.D22, R15.Pin_1, S1.Pin_3, S1.Pin_4, C7.1
  N17: Arduino_MEGA_2560.D24, C8.1, S2.Pin_3, S2.Pin_4, R16.Pin_1
  N18: LED5.anode, R9.Pin_0
  N19: LED2.anode, R7.Pin_0
  N20: U1.S, R1.Pin_1, C1.1
  N21: U2.S, R2.Pin_1, C2.1
  N22: U3.S, R3.Pin_1, C3.1
  N23: U4.S, R4.Pin_1, C4.1
  N24: U5.S, R5.Pin_1, C5.1
  N25: R6.Pin_1, U6.S, C6.1
  N26: R8.Pin_0, LED3.anode
  N27: R10.Pin_0, LED4.anode
  N28: R11.Pin_0, LED6.anode
  N29: R14.Pin_0, LED7.anode
  N30: LED1.anode, R12.Pin_0
